# Fritzing sketch Metal Detector #1 (saved by Fritzing 0.9.2b)
breadboards: 1

parts:
  part = 555 Timer [package="DIP8 [THT]"]
  part_2 = Electrolytic Capacitor [capacitance=1µF package="100 mil [THT, electrolytic]"]
  part_3 = Electrolytic Capacitor [capacitance=1µF package="100 mil [THT, electrolytic]"]
  part_4 = Resistor [tolerance=±5% resistance=220 package=THT]
  part_5 = Inductor [package="400 mil [THT]"]
  part_6 = Piezo Speaker

nets:
  N1: part.Ground, part_2.-, part_6.pin2
  N2: part.Trigger, part_2.+
  N3: part.Output, part_4.Pin_0, part_5.pin_1
  N4: part.Reset, part.Vcc_Supply_Voltage
  N5: part.Threshold, part_3.-, part_4.Pin_1
  N6: part_3.+, part_5.pin_0

notes:
  Gnd
  Vcc
