# Fritzing sketch Metal Detector #2 (saved by Fritzing 0.9.2b)
breadboards: 1

parts:
  22n = Ceramic Capacitor [capacitance=100nF package="100 mil [THT, multilayer]"]
  100n = Ceramic Capacitor [capacitance=100nF package="100 mil [THT, multilayer]"]
  22n_2 = Ceramic Capacitor [capacitance=100nF package="100 mil [THT, multilayer]"]
  10K = Resistor [tolerance=±5% resistance=220 package=THT]
  2n2222 = NPN-Transistor [package="TO92 [THT]"]
  L1 = Inductor [package="400 mil [THT]"]
  10K_2 = Resistor [tolerance=±5% resistance=220 package=THT]
  VR = Resistor [tolerance=±5% resistance=220 package=THT]

nets:
  N1: 22n.0, 22n_2.1, 2n2222.C, VR.Pin_1
  N2: 22n.1, 10K.Pin_1, L1.pin_0
  N3: 100n.0, 10K_2.Pin_0, VR.Pin_0
  N4: 100n.1, 10K.Pin_0, 2n2222.B, 10K_2.Pin_1
  N5: 22n_2.0, 2n2222.E, L1.pin_1

notes:
  Vcc
  Output
  Gnd
