# Fritzing sketch Pace Counter (saved by Fritzing 0.9.2b)
circuit board: 5.86951cm x 3.8453cm
breadboards: 1

parts:
  Mercury_Switch = Tilt Switch [package=THT]
  10_K = Resistor [tolerance=±5% resistance=220 package=THT]
  Buzzer = Piezo Speaker

nets:
  N1: Mercury_Switch.Pin_2, 10_K.Pin_1
  N2: 10_K.Pin_0, Buzzer.pin1

notes:
  Gnd
  D3
  D4
  Vcc
  D1
  D0
  Sck
  Rck
  Data
  D2
